# Fritzing sketch smartTemperatureMonitoring (saved by Fritzing 0.9.3b)
breadboards: 1

parts:
  M1 = ESP32-S3-DevKitC-1-N8R8-v1 [part_number=ESP32-S3-DevKitC-1-N8R8-v1]
  Componente2 = Arduino Uno (Rev3) - ICSP
  R5 = Rotary Potentiometer (Small) [maximum_resistance=100kΩ package=THT]
  S3 = Pushbutton [package="[SMD]"]
  Display2 = LCD screen 16x2 IIC [part_number=101290]
  J2 = Basic Servo
  R6 = Resistor [tolerance=±5% resistance=10k package="0603 [SMD]"]
  LED1 = smd LED [color="Red (633nm)" package="1206 [SMD]"]
  LED2 = smd LED [color="Green (555nm)" package="1206 [SMD]"]
  R7 = Resistor [tolerance=±5% resistance=220 package="1206 [SMD]"]
  R8 = Resistor [tolerance=±5% resistance=220 package="1206 [SMD]"]
  U1 = TMP36 [package=to-92]

nets:
  N1: M1.pin_1, M1.pin_2
  N2: M1.pin_4, R7.Pin_0
  N3: M1.pin_5, R8.Pin_0
  N4: M1.pin_21, U1.VCC
  N5: M1.pin_22, M1.pin_23, M1.pin_24, M1.pin_44, U1.GND
  N6: M1.pin_33, U1.VOUT
  N7: Componente2.A0, R5.wiper
  N8: Componente2.A4/SDA, Display2.SDA
  N9: Componente2.A5/SCL, Display2.SCL
  N10: Componente2.D9_PWM, J2.pulse
  N11: Componente2.D5_PWM, S3.Pin_1, S3.Pin_2, R6.Pin_0
  VCC: Componente2.5V, R5.leg1, S3.Pin_3, S3.Pin_4, Display2.VCC, J2.vcc, LED1.cathode, LED2.cathode
  GND: Componente2.GND, R5.leg2, Display2.GND, J2.gnd, R6.Pin_1
  N12: LED1.anode, R7.Pin_1
  N13: LED2.anode, R8.Pin_1

custom parts:
  ESP32-S3-DevKitC-1-N8R8-v1: ESP32-S3-DevKitC-1-N8R8-v1 This module is 44pins long (2x22) and 11 pins width.
  LCD screen 16x2 IIC: LCD screen with HD44780 controller enables showing text, symbols, value or anything else that comes from Croduino/Arduino. It is capable of showing 16 symbols in two lines and therefore can be used in many projects that need to send clearly visible and legible output information.. • Color of symbols: White • Backlight: Blue • Dimensions: 80 x 36 x 12 mm • Screen dimensions: 64.5 x 16 mm •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
