# Fritzing sketch temperature-monitoring (saved by Fritzing 0.9.3b)
breadboards: 1

parts:
  M1 = ESP32-S3-DevKitC-1-N8R8-v1 [part_number=ESP32-S3-DevKitC-1-N8R8-v1]
  LED1 = smd LED [color="Red (633nm)" package="1206 [SMD]"]
  LED2 = smd LED [color="Green (555nm)" package="1206 [SMD]"]
  R7 = Resistor [tolerance=±5% resistance=220 package="1206 [SMD]"]
  R8 = Resistor [tolerance=±5% resistance=220 package="1206 [SMD]"]
  U1 = TMP36 [package=to-92]

nets:
  N1: M1.pin_1, M1.pin_2
  N2: M1.pin_5, R7.Pin_0
  N3: M1.pin_6, R8.Pin_0
  N4: M1.pin_21, U1.VCC
  N5: M1.pin_22, M1.pin_23, M1.pin_24, M1.pin_44, U1.GND
  N6: M1.pin_33, U1.VOUT
  N7: LED1.cathode, LED2.cathode
  N8: LED1.anode, R7.Pin_1
  N9: LED2.anode, R8.Pin_1

custom parts:
  ESP32-S3-DevKitC-1-N8R8-v1: ESP32-S3-DevKitC-1-N8R8-v1 This module is 44pins long (2x22) and 11 pins width.
