# Fritzing sketch window-controller (saved by Fritzing 0.9.3b)
breadboards: 1

parts:
  Componente2 = Arduino Uno (Rev3) - ICSP
  R5 = Rotary Potentiometer (Small) [maximum_resistance=100kΩ package=THT]
  S3 = Pushbutton [package="[SMD]"]
  Display2 = LCD screen 16x2 IIC [part_number=101290]
  J2 = Basic Servo
  R6 = Resistor [tolerance=±5% resistance=10k package="0603 [SMD]"]

nets:
  N1: Componente2.A0, R5.wiper
  N2: Componente2.A4/SDA, Display2.SDA
  N3: Componente2.A5/SCL, Display2.SCL
  N4: Componente2.D9_PWM, J2.pulse
  N5: Componente2.D7, S3.Pin_3, S3.Pin_4
  VCC: Componente2.5V, R5.leg1, S3.Pin_1, S3.Pin_2, Display2.VCC, J2.vcc, R6.Pin_0
  GND: Componente2.GND, R5.leg2, Display2.GND, J2.gnd, R6.Pin_1

custom parts:
  LCD screen 16x2 IIC: LCD screen with HD44780 controller enables showing text, symbols, value or anything else that comes from Croduino/Arduino. It is capable of showing 16 symbols in two lines and therefore can be used in many projects that need to send clearly visible and legible output information.. • Color of symbols: White • Backlight: Blue • Dimensions: 80 x 36 x 12 mm • Screen dimensions: 64.5 x 16 mm •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
